// Logisim project branch-comp.circ as structural Verilog: 1 circuit, main circuit branch_comp
module branch_comp (
  input  [31:0] BrData1,
  input  [31:0] BrData2,
  input  BrUn,
  output BrEq,
  output BrLt
);

  wire beqs, bequ, blts, bltu;

  Comparator #(.width(32)) comparator_1 (.a(BrData1), .b(BrData2), .eq(beqs));  // open: gt, lt
  Comparator #(.mode("unsigned"), .width(32)) comparator_2 (.a(BrData1), .b(BrData2), .eq(bequ));  // open: gt, lt
  Comparator #(.width(32)) comparator_3 (.a(BrData1), .b(BrData2), .lt(blts));  // open: gt, eq
  Comparator #(.mode("unsigned"), .width(32)) comparator_4 (.a(BrData1), .b(BrData2), .lt(bltu));  // open: gt, eq
  Multiplexer #(.enable("false")) multiplexer_1 (.in0(beqs), .in1(bequ), .out(BrEq), .sel(BrUn));
  Multiplexer #(.enable("false")) multiplexer_2 (.in0(blts), .in1(bltu), .out(BrLt), .sel(BrUn));

  // Notes on the sheet:
  //   INPUTS to your circuit
  //   DON'T CHANGE THE LOCATIONS OF THE INPUTS AND OUTPUTS!
  //   OUTPUT from your circuit
endmodule
