// Logisim project control-logic.circ as structural Verilog: 1 circuit, main circuit control_logic
module control_logic (
  input  [31:0] Instruction,
  input  BrEq,
  input  BrLt,
  output PCSel,
  output RegWEn,
  output [2:0] ImmSel,
  output BrUn,
  output ASel,
  output BSel,
  output [3:0] ALUSel,
  output MemWEn,
  output [1:0] WBSel
);

  wire and_19_out, and_20_out, and_21_out, and_22_out, and_23_out, funct3_0, funct3_1, funct3_2, funct3_3,
       funct3_4, funct3_5, funct3_6, funct3_7, funct7_0, funct7_1, funct7_32, is_add, is_addi, is_and,
       is_andi, is_auipc, is_b, is_beq, is_bge, is_bgeu, is_blt, is_bltu, is_bne, is_i, is_iload, is_jalr,
       is_jump, is_lb, is_lh, is_lui, is_lw, is_mul, is_mulh, is_mulhu, is_or, is_ori, is_r, is_s, is_sb,
       is_sh, is_sll, is_slli, is_slt, is_slti, is_sra, is_srai, is_srl, is_srli, is_sub, is_sw, is_xor,
       is_xori, not_1_out, not_2_out, or_1_out, or_2_out, or_3_out, or_4_out, or_5_out, or_6_out,
       priority_encoder_1_en_out, r_add, r_and, r_mul, r_mulh, r_mulhu, r_or, r_sll, r_slt, r_sra, r_srl,
       r_sub, r_xor, srai, srli;
  wire [1:0] priority_encoder_2_out;
  wire [4:0] ROMinput1;
  wire [5:0] ROMinput, ROMinput2;
  wire [15:14] rom_1_data;

  ROM #(.addrWidth(6), .dataWidth(16)) rom_1 (
    .addr(ROMinput), .data({rom_1_data, WBSel, MemWEn, ALUSel, BSel, ASel, BrUn, ImmSel, RegWEn}));
  Comparator #(.width(7)) comparator_1 (.a(Instruction[31:25]), .b(7'b0000001), .eq(funct7_1));  // open: gt, lt
  Comparator #(.width(7)) comparator_2 (.a(Instruction[6:0]), .b(7'b1100011), .eq(is_b));  // open: gt, lt
  Comparator #(.width(7)) comparator_3 (.a(Instruction[6:0]), .b(7'b0000011), .eq(is_iload));  // open: gt, lt
  Comparator #(.width(7)) comparator_4 (.a(Instruction[6:0]), .b(7'b0100011), .eq(is_s));  // open: gt, lt
  Comparator #(.width(7)) comparator_5 (.a(Instruction[6:0]), .b(7'b1101111), .eq(is_jump));  // open: gt, lt
  Comparator #(.width(7)) comparator_6 (.a(Instruction[6:0]), .b(7'b1100111), .eq(is_jalr));  // open: gt, lt
  Comparator #(.width(7)) comparator_7 (.a(Instruction[6:0]), .b(7'b0010111), .eq(is_auipc));  // open: gt, lt
  Comparator #(.width(7)) comparator_8 (.a(Instruction[6:0]), .b(7'b0110111), .eq(is_lui));  // open: gt, lt
  Comparator #(.width(7)) comparator_9 (.a(Instruction[6:0]), .b(7'b0010011), .eq(is_i));  // open: gt, lt
  and and_1 (r_sll, funct3_1, funct7_0);
  and and_2 (r_srl, funct3_5, funct7_0);
  and and_3 (r_sra, funct3_5, funct7_32);
  and and_4 (r_slt, funct3_2, funct7_0);
  Comparator #(.width(7)) comparator_10 (.a(Instruction[6:0]), .b(7'b0110011), .eq(is_r));  // open: gt, lt
  Priority_Encoder #(.select(5)) priority_encoder_1 (
    .in0(is_add), .in1(is_mul), .in2(is_sub), .in3(is_sll), .in4(is_mulh), .in5(is_mulhu), .in6(is_slt),
    .in7(is_xor), .in8(is_srl), .in9(is_sra), .in10(is_or), .in11(is_and), .in12(is_lb), .in13(is_lh),
    .in14(is_lw), .in15(is_addi), .in16(is_slli), .in17(is_slti), .in18(is_xori), .in19(is_srli),
    .in20(is_srai), .in21(is_ori), .in22(is_andi), .in23(is_sb), .in24(is_sh), .in25(is_sw), .in26(is_beq),
    .in27(is_bne), .in28(is_blt), .in29(is_bge), .in30(is_bltu), .in31(is_bgeu), .out(ROMinput1),
    .en_out(priority_encoder_1_en_out));  // open: gs, en_in
  and and_5 (is_beq, is_b, funct3_0);
  and and_6 (is_lb, is_iload, funct3_0);
  and and_7 (is_sb, is_s, funct3_0);
  Comparator #(.width(3)) comparator_11 (.a(Instruction[14:12]), .b(3'b000), .eq(funct3_0));  // open: gt, lt
  Comparator #(.width(3)) comparator_12 (.a(Instruction[14:12]), .b(3'b111), .eq(funct3_7));  // open: gt, lt
  Comparator #(.width(3)) comparator_13 (.a(Instruction[14:12]), .b(3'b110), .eq(funct3_6));  // open: gt, lt
  Comparator #(.width(3)) comparator_14 (.a(Instruction[14:12]), .b(3'b100), .eq(funct3_4));  // open: gt, lt
  Comparator #(.width(3)) comparator_15 (.a(Instruction[14:12]), .b(3'b001), .eq(funct3_1));  // open: gt, lt
  Comparator #(.width(3)) comparator_16 (.a(Instruction[14:12]), .b(3'b010), .eq(funct3_2));  // open: gt, lt
  Comparator #(.width(3)) comparator_17 (.a(Instruction[14:12]), .b(3'b101), .eq(funct3_5));  // open: gt, lt
  Comparator #(.width(3)) comparator_18 (.a(Instruction[14:12]), .b(3'b011), .eq(funct3_3));  // open: gt, lt
  and and_8 (is_bge, is_b, funct3_5);
  and and_9 (is_lh, is_iload, funct3_1);
  and and_10 (is_sh, is_s, funct3_1);
  Priority_Encoder #(.select(2)) priority_encoder_2 (
    .in0(is_auipc), .in1(is_lui), .in2(is_jump), .in3(is_jalr), .out(priority_encoder_2_out));  // open: gs, en_out, en_in
  and and_11 (r_add, funct3_0, funct7_0);
  and and_12 (r_sub, funct3_0, funct7_32);
  and and_13 (r_and, funct3_7, funct7_0);
  and and_14 (r_or, funct3_6, funct7_0);
  and and_15 (r_xor, funct3_4, funct7_0);
  not not_1 (not_1_out, BrLt);
  or or_1 (or_1_out, is_bge, is_bgeu);
  not not_2 (not_2_out, BrEq);
  and and_16 (is_bgeu, is_b, funct3_7);
  and and_17 (is_lw, is_iload, funct3_2);
  and and_18 (is_sw, is_s, funct3_2);
  and and_19 (and_19_out, not_1_out, or_1_out);
  or or_2 (or_2_out, is_jump, is_jalr);
  and and_20 (and_20_out, BrEq, is_beq);
  and and_21 (and_21_out, not_2_out, is_bne);
  and and_22 (and_22_out, BrLt, is_blt);
  and and_23 (and_23_out, BrLt, is_bltu);
  and and_24 (is_addi, is_i, funct3_0);
  Comparator #(.width(7)) comparator_19 (.a(Instruction[31:25]), .b({7{1'b0}}), .eq(funct7_0));  // open: gt, lt
  Comparator #(.width(7)) comparator_20 (.a(Instruction[31:25]), .b(7'b0100000), .eq(funct7_32));  // open: gt, lt
  or or_3 (or_3_out, and_20_out, and_21_out);
  or or_4 (or_4_out, and_22_out, and_23_out);
  Multiplexer #(.enable("false"), .width(6)) multiplexer_1 (
    .in0({1'b0, ROMinput1}), .in1(ROMinput2), .out(ROMinput), .sel(priority_encoder_1_en_out));
  and and_25 (is_blt, is_b, funct3_4);
  or or_5 (or_5_out, or_3_out, or_4_out);
  Adder #(.width(6)) adder_1 (
    .a({4'b0000, priority_encoder_2_out}), .b(6'b100000), .out(ROMinput2));  // open: cin, cout
  and and_26 (is_andi, is_i, funct3_7);
  and and_27 (is_add, is_r, r_add);
  and and_28 (is_slt, is_r, r_slt);
  or or_6 (or_6_out, and_19_out, or_2_out);
  and and_29 (is_bltu, is_b, funct3_6);
  or or_7 (PCSel, or_6_out, or_5_out);
  and and_30 (is_ori, is_i, funct3_6);
  and and_31 (is_sub, is_r, r_sub);
  and and_32 (is_mul, is_r, r_mul);
  and and_33 (r_mul, funct3_0, funct7_1);
  and and_34 (r_mulh, funct3_1, funct7_1);
  and and_35 (r_mulhu, funct3_3, funct7_1);
  and and_36 (srli, funct3_5, funct7_0);
  and and_37 (srai, funct3_5, funct7_32);
  and and_38 (is_xori, is_i, funct3_4);
  and and_39 (is_and, is_r, r_and);
  and and_40 (is_mulh, is_r, r_mulh);
  and and_41 (is_bne, is_b, funct3_1);
  and and_42 (is_slli, is_i, funct3_1);
  and and_43 (is_or, is_r, r_or);
  and and_44 (is_mulhu, is_r, r_mulhu);
  and and_45 (is_srli, is_i, srli);
  and and_46 (is_xor, is_r, r_xor);
  and and_47 (is_slti, is_i, funct3_2);
  and and_48 (is_sll, is_r, r_sll);
  and and_49 (is_srai, is_i, srai);
  and and_50 (is_srl, is_r, r_srl);
  and and_51 (is_sra, is_r, r_sra);

  // Other names for the same wires on the sheet: opcode[6:0] = Instruction[6:0]; rd_imm[4:0] = Instruction[11:7];
  //   funct3[2:0] = Instruction[14:12]; rs1[4:0] = Instruction[19:15]; rs2_imm[4:0] = Instruction[24:20];
  //   imm_funct7[6:0] = Instruction[31:25]

  // Notes on the sheet:
  //   INPUTS to your circuit
  //   B-Type Instructions
  //   I-Type (Load) Instructions
  //   S-Type Instructions
  //   J-Type Instructions
  //   I-Type (jump) Instructions
  //   U-Type Instructions
  //   R-Type Instructions
  //   contents of rom_1 (hex, n*v repeats v):
  //   100b 140b 160b 108b 148b 158b 110b 120b 128b 168b 130b 138b 41 41 41 1041 10c1 1141 1241 12c1 16c1
  //   1341 13c1 842 842 842 4*64 74 74 1067 17c7 2069 2041
  //   Split Instruction into Components
  //   I-Type (non-load) Instructions
  //   ROM FOR CONTROL LOGIC
  //   DON'T CHANGE THE LOCATIONS OF THE INPUTS AND OUTPUTS!
  //   This is only if you choose to do the ROM option
  //   OUTPUT from your circuit
  //   Reminder: If using ROM, use combinational logic for PCSel
endmodule
