// Logisim project imm-gen.circ as structural Verilog: 1 circuit, main circuit imm_gen
module imm_gen (
  input  [31:0] Instruction,
  input  [2:0] ImmSel,
  output [31:0] Immediate
);

  wire [31:0] I_intermediate, J_intermediate, S_intermediate;
  wire [31:12] B_intermediate;

  assign B_intermediate = {{19{Instruction[31]}}, Instruction[31]};  // Bit_Extender bit_extender_1
  assign S_intermediate = {{20{Instruction[31]}}, {Instruction[31:25], Instruction[11:7]}};  // Bit_Extender bit_extender_2
  assign J_intermediate = {{11{Instruction[31]}}, {Instruction[31], Instruction[19:12], Instruction[20], Instruction[30:21], 1'b0}};  // Bit_Extender bit_extender_3
  assign I_intermediate = {{20{Instruction[31]}}, Instruction[31:20]};  // Bit_Extender bit_extender_4
  Multiplexer #(.enable("false"), .select(3), .width(32)) multiplexer_1 (
    .in0(I_intermediate), .in1(S_intermediate),
    .in2({B_intermediate, Instruction[7], Instruction[30:25], Instruction[11:8], 1'b0}),
    .in3({Instruction[31:12], {12{1'b0}}}), .in4(J_intermediate), .out(Immediate), .sel(ImmSel));  // open: in5, in6, in7

  // Other names for the same wires on the sheet: B_intermediate[11:1] = {Instruction[7], Instruction[30:25], Instruction[11:8]};
  //   U_intermediate[31:12] = Instruction[31:12]

  // Notes on the sheet:
  //   INPUTS to your circuit
  //   DON'T CHANGE THE LOCATIONS OF THE INPUTS AND OUTPUTS!
  //   OUTPUT from your circuit
endmodule
