// Logisim project partial-load.circ as structural Verilog: 1 circuit, main circuit partial_load
module partial_load (
  input  [31:0] Instruction,
  input  [31:0] MemAddress,
  input  [31:0] DataFromMem,
  output [31:0] DataToReg
);

  wire funct3_0, funct3_1, funct3_2, is_iload;
  wire [31:0] lb_bottom_8, lb_mid_bottom_8, lb_mid_top_8, lb_result, lb_top_8, lh_bottom_16, lh_middle_16,
       lh_result, lh_top_16;

  Comparator #(.width(7)) comparator_1 (.a(Instruction[6:0]), .b(7'b0000011), .eq(is_iload));  // open: gt, lt
  assign lb_top_8 = {{24{DataFromMem[7]}}, DataFromMem[7:0]};  // Bit_Extender bit_extender_1
  assign lb_mid_bottom_8 = {{24{DataFromMem[23]}}, DataFromMem[23:16]};  // Bit_Extender bit_extender_2
  assign lb_bottom_8 = {{24{DataFromMem[31]}}, DataFromMem[31:24]};  // Bit_Extender bit_extender_3
  assign lh_top_16 = {{16{DataFromMem[15]}}, DataFromMem[15:0]};  // Bit_Extender bit_extender_4
  assign lh_bottom_16 = {{16{DataFromMem[31]}}, DataFromMem[31:16]};  // Bit_Extender bit_extender_5
  assign lh_middle_16 = {{16{DataFromMem[23]}}, DataFromMem[23:8]};  // Bit_Extender bit_extender_6
  assign lb_mid_top_8 = {{24{DataFromMem[15]}}, DataFromMem[15:8]};  // Bit_Extender bit_extender_7
  Comparator #(.width(3)) comparator_2 (.a(Instruction[14:12]), .b(3'b000), .eq(funct3_0));  // open: gt, lt
  Comparator #(.width(3)) comparator_3 (.a(Instruction[14:12]), .b(3'b001), .eq(funct3_1));  // open: gt, lt
  Comparator #(.width(3)) comparator_4 (.a(Instruction[14:12]), .b(3'b010), .eq(funct3_2));  // open: gt, lt
  Multiplexer #(.enable("false"), .select(2), .width(32)) multiplexer_1 (
    .in0(lb_top_8), .in1(lb_mid_top_8), .in2(lb_mid_bottom_8), .in3(lb_bottom_8), .out(lb_result),
    .sel(MemAddress[1:0]));
  Multiplexer #(.enable("false"), .select(2), .width(32)) multiplexer_2 (
    .in0(lh_top_16), .in1(lh_middle_16), .in2(lh_bottom_16), .out(lh_result), .sel(MemAddress[1:0]));  // open: in3
  Multiplexer #(.enable("false"), .select(3), .width(32)) multiplexer_3 (
    .in0(lb_result), .in1(lh_result), .in2(DataFromMem), .out(DataToReg), .sel(Instruction[14:12]));  // open: in3, in4, in5, in6, in7

  // Other names for the same wires on the sheet: opcode[6:0] = Instruction[6:0]; funct3[2:0] = Instruction[14:12];
  //   bottom2bits[1:0] = MemAddress[1:0]

  // Notes on the sheet:
  //   INPUTS to your circuit
  //   lb Instruction
  //   DON'T CHANGE THE LOCATIONS OF THE INPUTS AND OUTPUTS!
  //   OUTPUT from your circuit
endmodule
