// Logisim project partial-store.circ as structural Verilog: 1 circuit, main circuit partial_store
module partial_store (
  input  [31:0] Instruction,
  input  [31:0] MemAddress,
  input  [31:0] DataFromReg,
  input  MemWEn,
  output [3:0] MemWriteMask,
  output [31:0] DataToMem
);

  wire bottom_0, bottom_1, bottom_2, bottom_3, funct3_0, funct3_1, funct3_2, mask1, mask2, mask3, mask4,
       mask8, mask12, mask15;
  wire [31:0] sb_result, sh_result;

  Comparator #(.width(3)) comparator_1 (.a(Instruction[14:12]), .b(3'b000), .eq(funct3_0));  // open: gt, lt
  Comparator #(.width(3)) comparator_2 (.a(Instruction[14:12]), .b(3'b001), .eq(funct3_1));  // open: gt, lt
  Comparator #(.width(3)) comparator_3 (.a(Instruction[14:12]), .b(3'b010), .eq(funct3_2));  // open: gt, lt
  Multiplexer #(.enable("false"), .select(2), .width(32)) multiplexer_1 (
    .in0({{16{1'b0}}, DataFromReg[15:0]}), .in2({DataFromReg[15:0], {16{1'b0}}}), .out(sh_result),
    .sel(MemAddress[1:0]));  // open: in1, in3
  Comparator #(.width(2)) comparator_4 (.a(MemAddress[1:0]), .b(2'b00), .eq(bottom_0));  // open: gt, lt
  Comparator #(.width(2)) comparator_5 (.a(MemAddress[1:0]), .b(2'b01), .eq(bottom_1));  // open: gt, lt
  Comparator #(.width(2)) comparator_6 (.a(MemAddress[1:0]), .b(2'b10), .eq(bottom_2));  // open: gt, lt
  Comparator #(.width(2)) comparator_7 (.a(MemAddress[1:0]), .b(2'b11), .eq(bottom_3));  // open: gt, lt
  Multiplexer #(.enable("false"), .select(2), .width(32)) multiplexer_2 (
    .in0({{24{1'b1}}, DataFromReg[7:0]}), .in1({{16{1'b1}}, DataFromReg[7:0], {8{1'b1}}}),
    .in2({{8{1'b1}}, DataFromReg[7:0], {16{1'b1}}}), .in3({DataFromReg[7:0], {24{1'b1}}}), .out(sb_result),
    .sel(MemAddress[1:0]));
  and and_1 (mask1, funct3_0, bottom_0);
  and and_2 (mask2, funct3_0, bottom_1);
  and and_3 (mask4, funct3_0, bottom_2);
  and and_4 (mask8, funct3_0, bottom_3);
  and and_5 (mask3, funct3_1, bottom_0);
  and and_6 (mask12, funct3_1, bottom_2);
  and and_7 (mask15, funct3_2, bottom_0);
  Multiplexer #(.enable("false"), .select(3), .width(32)) multiplexer_3 (
    .in0(sb_result), .in1(sh_result), .in2(DataFromReg), .out(DataToMem), .sel(Instruction[14:12]));  // open: in3, in4, in5, in6, in7
  Priority_Encoder #(.select(4)) priority_encoder_1 (
    .in1(mask1), .in2(mask2), .in3(mask3), .in4(mask4), .in8(mask8), .in12(mask12), .in15(mask15),
    .out(MemWriteMask), .en_in(MemWEn));  // open: in0, in5, in6, in7, in9, in10, in11, in13, in14, gs, en_out

  // Other names for the same wires on the sheet: opcode[6:0] = Instruction[6:0]; funct3[2:0] = Instruction[14:12];
  //   bottom2bits[1:0] = MemAddress[1:0]; reg7[7:0] = DataFromReg[7:0]; reg16[15:0] = DataFromReg[15:0];
  //   sb_bottom[31:24] = DataFromReg[7:0]; sb_mid1[15:8] = DataFromReg[7:0]; sb_mid2[23:16] = DataFromReg[7:0];
  //   sb_top[7:0] = DataFromReg[7:0]; sh_bottom[31:16] = DataFromReg[15:0]; sh_top[15:0] = DataFromReg[15:0]

  // Notes on the sheet:
  //   INPUTS to your circuit
  //   DON'T CHANGE THE LOCATIONS OF THE INPUTS AND OUTPUTS!
  //   OUTPUT from your circuit
endmodule
