// Logisim project regfile.circ as structural Verilog: 3 circuits, main circuit regfile
module regfile (
  input  [4:0] ReadReg1,
  input  [4:0] ReadReg2,
  input  [4:0] WriteReg,
  input  [31:0] RegWriteData,
  input  RegWEn,
  input  clk,
  output [31:0] ra,
  output [31:0] sp,
  output [31:0] t0,
  output [31:0] t1,
  output [31:0] t2,
  output [31:0] s0,
  output [31:0] s1,
  output [31:0] a0,
  output [31:0] RegReadData1,
  output [31:0] RegReadData2
);

  wire and_1_out, and_2_out, and_3_out, and_4_out, and_5_out, and_6_out, and_7_out, and_8_out, and_9_out,
       and_10_out, and_11_out, and_12_out, and_13_out, and_14_out, and_15_out, and_16_out, and_17_out,
       and_18_out, and_19_out, and_20_out, and_21_out, and_22_out, and_23_out, and_24_out, and_25_out,
       and_26_out, and_27_out, and_28_out, and_29_out, and_30_out, and_31_out, and_32_out, decoder_1_out0,
       decoder_1_out1, decoder_1_out2, decoder_1_out3, decoder_1_out4, decoder_1_out5, decoder_1_out6,
       decoder_1_out7, decoder_1_out8, decoder_1_out9, decoder_1_out10, decoder_1_out11, decoder_1_out12,
       decoder_1_out13, decoder_1_out14, decoder_1_out15, decoder_1_out16, decoder_1_out17, decoder_1_out18,
       decoder_1_out19, decoder_1_out20, decoder_1_out21, decoder_1_out22, decoder_1_out23, decoder_1_out24,
       decoder_1_out25, decoder_1_out26, decoder_1_out27, decoder_1_out28, decoder_1_out29, decoder_1_out30,
       decoder_1_out31;
  wire [31:0] register_1_q, register_4_q, register_5_q, register_12_q, register_13_q, register_14_q,
       register_15_q, register_16_q, register_17_q, register_18_q, register_19_q, register_20_q,
       register_21_q, register_22_q, register_23_q, register_24_q, register_25_q, register_26_q,
       register_27_q, register_28_q, register_29_q, register_30_q, register_31_q, register_32_q;

  Decoder #(.select(5)) decoder_1 (
    .out0(decoder_1_out0), .out1(decoder_1_out1), .out2(decoder_1_out2), .out3(decoder_1_out3),
    .out4(decoder_1_out4), .out5(decoder_1_out5), .out6(decoder_1_out6), .out7(decoder_1_out7),
    .out8(decoder_1_out8), .out9(decoder_1_out9), .out10(decoder_1_out10), .out11(decoder_1_out11),
    .out12(decoder_1_out12), .out13(decoder_1_out13), .out14(decoder_1_out14), .out15(decoder_1_out15),
    .out16(decoder_1_out16), .out17(decoder_1_out17), .out18(decoder_1_out18), .out19(decoder_1_out19),
    .out20(decoder_1_out20), .out21(decoder_1_out21), .out22(decoder_1_out22), .out23(decoder_1_out23),
    .out24(decoder_1_out24), .out25(decoder_1_out25), .out26(decoder_1_out26), .out27(decoder_1_out27),
    .out28(decoder_1_out28), .out29(decoder_1_out29), .out30(decoder_1_out30), .out31(decoder_1_out31),
    .sel(WriteReg));  // open: en
  and and_1 (and_1_out, decoder_1_out0, 1'b0);
  and and_2 (and_2_out, decoder_1_out1, RegWEn);
  and and_3 (and_3_out, decoder_1_out2, RegWEn);
  and and_4 (and_4_out, decoder_1_out3, RegWEn);
  and and_5 (and_5_out, decoder_1_out4, RegWEn);
  and and_6 (and_6_out, decoder_1_out5, RegWEn);
  and and_7 (and_7_out, decoder_1_out6, RegWEn);
  and and_8 (and_8_out, decoder_1_out7, RegWEn);
  Register #(.width(32)) register_1 (.D(RegWriteData), .en(and_1_out), .clk(clk), .Q(register_1_q));  // open: clr
  Register #(.width(32)) register_2 (.D(RegWriteData), .en(and_2_out), .clk(clk), .Q(ra));  // open: clr
  Register #(.width(32)) register_3 (.D(RegWriteData), .en(and_3_out), .clk(clk), .Q(sp));  // open: clr
  Register #(.width(32)) register_4 (.D(RegWriteData), .en(and_4_out), .clk(clk), .Q(register_4_q));  // open: clr
  Register #(.width(32)) register_5 (.D(RegWriteData), .en(and_5_out), .clk(clk), .Q(register_5_q));  // open: clr
  Register #(.width(32)) register_6 (.D(RegWriteData), .en(and_6_out), .clk(clk), .Q(t0));  // open: clr
  Register #(.width(32)) register_7 (.D(RegWriteData), .en(and_7_out), .clk(clk), .Q(t1));  // open: clr
  Register #(.width(32)) register_8 (.D(RegWriteData), .en(and_8_out), .clk(clk), .Q(t2));  // open: clr
  and and_9 (and_9_out, decoder_1_out8, RegWEn);
  and and_10 (and_10_out, decoder_1_out9, RegWEn);
  and and_11 (and_11_out, decoder_1_out10, RegWEn);
  and and_12 (and_12_out, decoder_1_out11, RegWEn);
  and and_13 (and_13_out, decoder_1_out12, RegWEn);
  and and_14 (and_14_out, decoder_1_out13, RegWEn);
  and and_15 (and_15_out, decoder_1_out14, RegWEn);
  and and_16 (and_16_out, decoder_1_out15, RegWEn);
  Register #(.width(32)) register_9 (.D(RegWriteData), .en(and_9_out), .clk(clk), .Q(s0));  // open: clr
  Register #(.width(32)) register_10 (.D(RegWriteData), .en(and_10_out), .clk(clk), .Q(s1));  // open: clr
  Register #(.width(32)) register_11 (.D(RegWriteData), .en(and_11_out), .clk(clk), .Q(a0));  // open: clr
  Register #(.width(32)) register_12 (.D(RegWriteData), .en(and_12_out), .clk(clk), .Q(register_12_q));  // open: clr
  Register #(.width(32)) register_13 (.D(RegWriteData), .en(and_13_out), .clk(clk), .Q(register_13_q));  // open: clr
  Register #(.width(32)) register_14 (.D(RegWriteData), .en(and_14_out), .clk(clk), .Q(register_14_q));  // open: clr
  Register #(.width(32)) register_15 (.D(RegWriteData), .en(and_15_out), .clk(clk), .Q(register_15_q));  // open: clr
  Register #(.width(32)) register_16 (.D(RegWriteData), .en(and_16_out), .clk(clk), .Q(register_16_q));  // open: clr
  and and_17 (and_17_out, decoder_1_out16, RegWEn);
  and and_18 (and_18_out, decoder_1_out17, RegWEn);
  and and_19 (and_19_out, decoder_1_out18, RegWEn);
  and and_20 (and_20_out, decoder_1_out19, RegWEn);
  and and_21 (and_21_out, decoder_1_out20, RegWEn);
  and and_22 (and_22_out, decoder_1_out21, RegWEn);
  and and_23 (and_23_out, decoder_1_out22, RegWEn);
  and and_24 (and_24_out, decoder_1_out23, RegWEn);
  Register #(.width(32)) register_17 (.D(RegWriteData), .en(and_17_out), .clk(clk), .Q(register_17_q));  // open: clr
  Register #(.width(32)) register_18 (.D(RegWriteData), .en(and_18_out), .clk(clk), .Q(register_18_q));  // open: clr
  Register #(.width(32)) register_19 (.D(RegWriteData), .en(and_19_out), .clk(clk), .Q(register_19_q));  // open: clr
  Register #(.width(32)) register_20 (.D(RegWriteData), .en(and_20_out), .clk(clk), .Q(register_20_q));  // open: clr
  Register #(.width(32)) register_21 (.D(RegWriteData), .en(and_21_out), .clk(clk), .Q(register_21_q));  // open: clr
  Register #(.width(32)) register_22 (.D(RegWriteData), .en(and_22_out), .clk(clk), .Q(register_22_q));  // open: clr
  Register #(.width(32)) register_23 (.D(RegWriteData), .en(and_23_out), .clk(clk), .Q(register_23_q));  // open: clr
  Register #(.width(32)) register_24 (.D(RegWriteData), .en(and_24_out), .clk(clk), .Q(register_24_q));  // open: clr
  and and_25 (and_25_out, decoder_1_out24, RegWEn);
  and and_26 (and_26_out, decoder_1_out25, RegWEn);
  and and_27 (and_27_out, decoder_1_out26, RegWEn);
  and and_28 (and_28_out, decoder_1_out27, RegWEn);
  and and_29 (and_29_out, decoder_1_out28, RegWEn);
  and and_30 (and_30_out, decoder_1_out29, RegWEn);
  and and_31 (and_31_out, decoder_1_out30, RegWEn);
  and and_32 (and_32_out, decoder_1_out31, RegWEn);
  Register #(.width(32)) register_25 (.D(RegWriteData), .en(and_25_out), .clk(clk), .Q(register_25_q));  // open: clr
  Register #(.width(32)) register_26 (.D(RegWriteData), .en(and_26_out), .clk(clk), .Q(register_26_q));  // open: clr
  Register #(.width(32)) register_27 (.D(RegWriteData), .en(and_27_out), .clk(clk), .Q(register_27_q));  // open: clr
  Register #(.width(32)) register_28 (.D(RegWriteData), .en(and_28_out), .clk(clk), .Q(register_28_q));  // open: clr
  Register #(.width(32)) register_29 (.D(RegWriteData), .en(and_29_out), .clk(clk), .Q(register_29_q));  // open: clr
  Register #(.width(32)) register_30 (.D(RegWriteData), .en(and_30_out), .clk(clk), .Q(register_30_q));  // open: clr
  Register #(.width(32)) register_31 (.D(RegWriteData), .en(and_31_out), .clk(clk), .Q(register_31_q));  // open: clr
  Register #(.width(32)) register_32 (.D(RegWriteData), .en(and_32_out), .clk(clk), .Q(register_32_q));  // open: clr
  Multiplexer #(.enable("false"), .select(5), .width(32)) multiplexer_1 (
    .in0(register_1_q), .in1(ra), .in2(sp), .in3(register_4_q), .in4(register_5_q), .in5(t0), .in6(t1),
    .in7(t2), .in8(s0), .in9(s1), .in10(a0), .in11(register_12_q), .in12(register_13_q),
    .in13(register_14_q), .in14(register_15_q), .in15(register_16_q), .in16(register_17_q),
    .in17(register_18_q), .in18(register_19_q), .in19(register_20_q), .in20(register_21_q),
    .in21(register_22_q), .in22(register_23_q), .in23(register_24_q), .in24(register_25_q),
    .in25(register_26_q), .in26(register_27_q), .in27(register_28_q), .in28(register_29_q),
    .in29(register_30_q), .in30(register_31_q), .in31(register_32_q), .out(RegReadData2), .sel(ReadReg2));
  Multiplexer #(.enable("false"), .select(5), .width(32)) multiplexer_2 (
    .in0(register_1_q), .in1(ra), .in2(sp), .in3(register_4_q), .in4(register_5_q), .in5(t0), .in6(t1),
    .in7(t2), .in8(s0), .in9(s1), .in10(a0), .in11(register_12_q), .in12(register_13_q),
    .in13(register_14_q), .in14(register_15_q), .in15(register_16_q), .in16(register_17_q),
    .in17(register_18_q), .in18(register_19_q), .in19(register_20_q), .in20(register_21_q),
    .in21(register_22_q), .in22(register_23_q), .in23(register_24_q), .in24(register_25_q),
    .in25(register_26_q), .in26(register_27_q), .in27(register_28_q), .in28(register_29_q),
    .in29(register_30_q), .in30(register_31_q), .in31(register_32_q), .out(RegReadData1), .sel(ReadReg1));

  // Notes on the sheet:
  //   INPUTS to your circuit
  //   DON'T CHANGE THE LOCATIONS OF THE INPUTS AND OUTPUTS!
  //   These are DEBUG/TEST outputs from your circuit.
  //   OUTPUTS from your circuit
endmodule

module oldregister (
);

  wire and_1_out, and_2_out, and_3_out, and_4_out, and_5_out, and_6_out, and_7_out, and_8_out,
       multiplexer_3_p9, multiplexer_3_p11;
  wire [4:0] ReadReg1, undriven_4, undriven_5;
  wire [31:0] a0, a1, a2, a3, a4, a5, a6, a7, gp, multiplexer_1_out, multiplexer_2_out, multiplexer_3_p1,
       multiplexer_3_p2, multiplexer_3_p3, multiplexer_3_p4, multiplexer_3_p5, multiplexer_3_p6,
       multiplexer_3_p7, multiplexer_3_p8, multiplexer_4_out, ra, s0, s1, s2, s3, s4, s5, s6, s7, s8, s9, sp,
       t0, t1, t2, t4, t5, t6, tp, undriven, undriven_2, undriven_3, undriven_6, undriven_7;

  Multiplexer #(.enable("false"), .select(5), .width(32)) multiplexer_1 (
    .in0(undriven_6), .in1(ra), .in2(sp), .in3(gp), .in4(tp), .in5(t0), .in6(t1), .in7(t2), .in8(s0),
    .in9(s1), .in10(a0), .in11(a1), .in12(a2), .in13(a3), .in14(a4), .in15(a5), .in16(a6), .in17(a7),
    .in18(s2), .in19(s3), .in20(s4), .in21(s5), .in22(s6), .in23(s7), .in24(s8), .in25(s9), .in26(undriven),
    .in27(undriven_2), .in28(undriven_3), .in29(t4), .in30(t5), .in31(t6), .out(multiplexer_1_out),
    .sel(undriven_4));
  Multiplexer #(.enable("false"), .select(5), .width(32)) multiplexer_2 (
    .in1(multiplexer_3_p1), .in2(multiplexer_3_p2), .in5(multiplexer_3_p3), .in6(multiplexer_3_p4),
    .in7(multiplexer_3_p5), .in8(multiplexer_3_p6), .in9(multiplexer_3_p7), .in10(multiplexer_3_p8),
    .out(multiplexer_2_out), .sel(undriven_5));  // open: in0, in3, in4, in11, in12, in13, in14, in15, in16, in17, in18, in19, in20, in21, in22, in23, in24, in25, in26, in27, in28, in29, in30, in31
  // Multiplexer #(.enable("false"), .select(5), .width(32)) multiplexer_3: pin names not known; wires that end beside it: multiplexer_3_p1, multiplexer_3_p2, multiplexer_3_p3, multiplexer_3_p4, multiplexer_3_p5, multiplexer_3_p6, multiplexer_3_p7, multiplexer_3_p8, multiplexer_3_p9, multiplexer_3_p9, multiplexer_3_p11, multiplexer_3_p11
  // AND_Gate and_1 has open pins: out=and_1_out
  // AND_Gate and_2 has open pins: out=and_2_out
  // AND_Gate and_3 has open pins: out=and_3_out
  // AND_Gate and_4 has open pins: out=and_4_out
  // AND_Gate and_5 has open pins: out=and_5_out
  // AND_Gate and_6 has open pins: out=and_6_out
  // AND_Gate and_7 has open pins: out=and_7_out
  // AND_Gate and_8 has open pins: out=and_8_out
  Register #(.width(32)) register_1 (.en(and_2_out));  // open: D, clk, Q, clr
  Register #(.width(32)) register_2 (.D(undriven_7), .en(and_3_out));  // open: clk, Q, clr
  Register #(.width(32)) register_3 (.D(undriven_7), .en(and_4_out));  // open: clk, Q, clr
  Register #(.width(32)) register_4 (.D(undriven_7), .en(and_5_out));  // open: clk, Q, clr
  Register #(.width(32)) register_5 (.D(undriven_7), .en(and_6_out));  // open: clk, Q, clr
  Register #(.width(32)) register_6 (.D(undriven_7), .en(and_7_out));  // open: clk, Q, clr
  Register #(.width(32)) register_7 (.D(undriven_7), .en(and_8_out));  // open: clk, Q, clr
  Multiplexer #(.enable("false"), .select(5), .width(32)) multiplexer_4 (
    .in1(ra), .in2(sp), .in5(t0), .in6(t1), .in7(t2), .in8(s0), .in9(s1), .in10(a0), .out(multiplexer_4_out),
    .sel(ReadReg1));  // open: in0, in3, in4, in11, in12, in13, in14, in15, in16, in17, in18, in19, in20, in21, in22, in23, in24, in25, in26, in27, in28, in29, in30, in31
endmodule

module hi (
);

  wire and_1_out, and_2_out, and_3_out, and_4_out, and_5_out, and_6_out, and_7_out, and_8_out, and_9_out,
       and_10_out, and_11_out, and_12_out, and_13_out, and_14_out, and_15_out, and_16_out, and_17_out,
       and_18_out, and_19_out, and_20_out, and_21_out, and_22_out, and_23_out, and_24_out, and_25_out,
       and_26_out, and_27_out, and_28_out, and_29_out, and_30_out, and_31_out, and_32_out, undriven,
       undriven_2, undriven_3, undriven_4, undriven_5, undriven_6, undriven_7, undriven_8, undriven_9,
       undriven_10, undriven_11, undriven_12, undriven_13, undriven_14, undriven_15, undriven_16,
       undriven_17, undriven_18, undriven_19, undriven_20, undriven_21, undriven_22, undriven_23,
       undriven_24, undriven_25, undriven_27, undriven_28, undriven_29, undriven_30, undriven_31,
       undriven_32, undriven_33, undriven_34, undriven_35, undriven_36;
  wire [4:0] undriven_39, undriven_40;
  wire [31:0] multiplexer_1_out, multiplexer_2_out, register_1_q, register_3_q, register_4_q, register_5_q,
       register_6_q, register_7_q, register_8_q, register_9_q, register_11_q, register_12_q, register_13_q,
       register_14_q, register_15_q, register_16_q, register_17_q, register_18_q, register_19_q,
       register_20_q, register_21_q, register_22_q, register_23_q, register_24_q, register_25_q,
       register_26_q, register_27_q, register_28_q, register_31_q, register_32_q, undriven_26, undriven_37,
       undriven_38;

  and and_1 (and_1_out, undriven_23, undriven_28);
  and and_2 (and_2_out, undriven_25, undriven_28);
  and and_3 (and_3_out, undriven_24, undriven_28);
  and and_4 (and_4_out, undriven_22, undriven_28);
  and and_5 (and_5_out, undriven_21, undriven_28);
  and and_6 (and_6_out, undriven_20, undriven_28);
  and and_7 (and_7_out, undriven_19, undriven_28);
  and and_8 (and_8_out, undriven_18, undriven_28);
  Register #(.width(32)) register_1 (
    .D(undriven_26), .en(and_1_out), .clk(undriven_27), .Q(register_1_q));  // open: clr
  Register #(.width(32)) register_2 (.en(and_2_out), .clk(undriven_27), .Q(register_1_q));  // open: D, clr
  Register #(.width(32)) register_3 (
    .D(undriven_26), .en(and_3_out), .clk(undriven_27), .Q(register_3_q));  // open: clr
  Register #(.width(32)) register_4 (
    .D(undriven_26), .en(and_4_out), .clk(undriven_27), .Q(register_4_q));  // open: clr
  Register #(.width(32)) register_5 (
    .D(undriven_26), .en(and_5_out), .clk(undriven_27), .Q(register_5_q));  // open: clr
  Register #(.width(32)) register_6 (
    .D(undriven_26), .en(and_6_out), .clk(undriven_27), .Q(register_6_q));  // open: clr
  Register #(.width(32)) register_7 (
    .D(undriven_26), .en(and_7_out), .clk(undriven_27), .Q(register_7_q));  // open: clr
  Register #(.width(32)) register_8 (
    .D(undriven_26), .en(and_8_out), .clk(undriven_27), .Q(register_8_q));  // open: clr
  and and_9 (and_9_out, undriven_16, undriven_28);
  and and_10 (and_10_out, undriven_14, undriven_28);
  and and_11 (and_11_out, undriven_12, undriven_28);
  and and_12 (and_12_out, undriven_10, undriven_28);
  and and_13 (and_13_out, undriven_8, undriven_28);
  and and_14 (and_14_out, undriven_6, undriven_28);
  and and_15 (and_15_out, undriven_4, undriven_28);
  and and_16 (and_16_out, undriven_2, undriven_28);
  Register #(.width(32)) register_9 (
    .D(undriven_26), .en(and_9_out), .clk(undriven_27), .Q(register_9_q));  // open: clr
  Register #(.width(32)) register_10 (
    .D(undriven_26), .en(and_10_out), .clk(undriven_27), .Q(register_3_q));  // open: clr
  Register #(.width(32)) register_11 (.D(undriven_26), .en(and_11_out), .Q(register_11_q));  // open: clk, clr
  Register #(.width(32)) register_12 (.D(undriven_26), .en(and_12_out), .Q(register_12_q));  // open: clk, clr
  Register #(.width(32)) register_13 (.D(undriven_26), .en(and_13_out), .Q(register_13_q));  // open: clk, clr
  Register #(.width(32)) register_14 (.D(undriven_26), .en(and_14_out), .Q(register_14_q));  // open: clk, clr
  Register #(.width(32)) register_15 (.D(undriven_26), .en(and_15_out), .Q(register_15_q));  // open: clk, clr
  Register #(.width(32)) register_16 (.D(undriven_26), .en(and_16_out), .Q(register_16_q));  // open: clk, clr
  and and_17 (and_17_out, undriven_17, undriven_28);
  and and_18 (and_18_out, undriven_15, undriven_28);
  and and_19 (and_19_out, undriven_13, undriven_28);
  and and_20 (and_20_out, undriven_11, undriven_28);
  and and_21 (and_21_out, undriven_9, undriven_28);
  and and_22 (and_22_out, undriven_7, undriven_28);
  and and_23 (and_23_out, undriven_5, undriven_28);
  and and_24 (and_24_out, undriven_3, undriven_28);
  Register #(.width(32)) register_17 (
    .D(undriven_26), .en(and_17_out), .clk(undriven_29), .Q(register_17_q));  // open: clr
  Register #(.width(32)) register_18 (.D(undriven_26), .en(and_18_out), .Q(register_18_q));  // open: clk, clr
  Register #(.width(32)) register_19 (.D(undriven_26), .en(and_19_out), .Q(register_19_q));  // open: clk, clr
  Register #(.width(32)) register_20 (.D(undriven_26), .en(and_20_out), .Q(register_20_q));  // open: clk, clr
  Register #(.width(32)) register_21 (.D(undriven_26), .en(and_21_out), .Q(register_21_q));  // open: clk, clr
  Register #(.width(32)) register_22 (.D(undriven_26), .en(and_22_out), .Q(register_22_q));  // open: clk, clr
  Register #(.width(32)) register_23 (.D(undriven_26), .en(and_23_out), .Q(register_23_q));  // open: clk, clr
  Register #(.width(32)) register_24 (.D(undriven_26), .en(and_24_out), .Q(register_24_q));  // open: clk, clr
  and and_25 (and_25_out, undriven, undriven_28);
  and and_26 (and_26_out, undriven_36, undriven_28);
  and and_27 (and_27_out, undriven_35, undriven_28);
  and and_28 (and_28_out, undriven_34, undriven_28);
  and and_29 (and_29_out, undriven_33, undriven_28);
  and and_30 (and_30_out, undriven_32, undriven_28);
  and and_31 (and_31_out, undriven_31, undriven_28);
  and and_32 (and_32_out, undriven_30, undriven_28);
  Register #(.width(32)) register_25 (
    .D(undriven_26), .en(and_25_out), .clk(undriven_27), .Q(register_25_q));  // open: clr
  Register #(.width(32)) register_26 (
    .D(undriven_26), .en(and_26_out), .clk(undriven_27), .Q(register_26_q));  // open: clr
  Register #(.width(32)) register_27 (
    .D(undriven_26), .en(and_27_out), .clk(undriven_27), .Q(register_27_q));  // open: clr
  Register #(.width(32)) register_28 (
    .D(undriven_26), .en(and_28_out), .clk(undriven_27), .Q(register_28_q));  // open: clr
  Register #(.width(32)) register_29 (
    .D(undriven_26), .en(and_29_out), .clk(undriven_27), .Q(register_1_q));  // open: clr
  Register #(.width(32)) register_30 (
    .D(undriven_26), .en(and_30_out), .clk(undriven_27), .Q(register_1_q));  // open: clr
  Register #(.width(32)) register_31 (
    .D(undriven_26), .en(and_31_out), .clk(undriven_27), .Q(register_31_q));  // open: clr
  Register #(.width(32)) register_32 (
    .D(undriven_26), .en(and_32_out), .clk(undriven_27), .Q(register_32_q));  // open: clr
  Multiplexer #(.enable("false"), .select(5), .width(32)) multiplexer_1 (
    .in0(register_1_q), .in1(register_1_q), .in2(undriven_38), .in3(register_1_q), .in4(register_5_q),
    .in5(undriven_37), .in6(register_7_q), .in7(register_8_q), .in8(register_9_q), .in9(register_3_q),
    .in10(register_11_q), .in11(register_12_q), .in12(register_13_q), .in13(register_14_q),
    .in14(register_15_q), .in15(register_16_q), .in16(register_17_q), .in17(register_18_q),
    .in18(register_19_q), .in19(register_20_q), .in20(register_21_q), .in21(register_22_q),
    .in22(register_23_q), .in23(register_24_q), .in24(register_25_q), .in25(register_26_q),
    .in26(register_27_q), .in27(register_28_q), .in30(register_31_q), .in31(register_32_q),
    .out(multiplexer_1_out), .sel(undriven_40));  // open: in28, in29
  Multiplexer #(.enable("false"), .select(5), .width(32)) multiplexer_2 (
    .in0(register_1_q), .in1(register_1_q), .in2(register_1_q), .in3(register_5_q), .in4(undriven_37),
    .in5(register_7_q), .in6(register_8_q), .in7(register_9_q), .in8(register_9_q), .in9(register_3_q),
    .in10(register_11_q), .in11(register_12_q), .in12(register_13_q), .in13(register_14_q),
    .in14(register_15_q), .in15(register_16_q), .in16(register_17_q), .in17(register_18_q),
    .in18(register_19_q), .in19(register_20_q), .in20(register_21_q), .in21(register_22_q),
    .in22(register_23_q), .in23(register_24_q), .in24(register_25_q), .in25(register_26_q),
    .in26(register_27_q), .in27(register_28_q), .in28(register_1_q), .in29(register_1_q),
    .in30(register_31_q), .in31(register_32_q), .out(multiplexer_2_out), .sel(undriven_39));
endmodule
